# Fritzing sketch 4655BrewCoStirPlate (saved by Fritzing 0.9.3b)
breadboards: 1

parts:
  Part1 = Spark Core (v1.0)
  12V_-_IN = Breadboard Power Supply Board SMD
  F1 = Fan - Ventilador [package=THT]
  R1 = Resistor [tolerance=±5% resistance=1k package=THT]
  D1 = Rectifier Diode [part_number=1N4001 package="300 mil [THT]"]
  C1 = Tantalum Capacitor [capacitance=1μF package="100 mil [THT, tantalum]"]
  R2 = Rotary Potentiometer (Small) [maximum_resistance=100kΩ package=THT]
  Q1 = TIP120 Hi-Current Darlington Transistor
  DHT1 = DHT22 Humidity and Temperature Sensor
  R3 = Resistor [tolerance=±5% resistance=10k package=THT]

nets:
  N1: Part1.A0, R2.wiper
  N2: Part1.A7, R1.Pin_0
  GND: Part1.GND, 12V_-_IN.GND, R2.leg1, DHT1.GND
  VIN: Part1.VIN, 12V_-_IN.VCC, R2.leg2, DHT1.VDD, R3.Pin_0
  N3: Part1.D4, DHT1.DATA, R3.Pin_1
  VIN_2: 12V_-_IN.VIN, F1.5V, C1.+
  N4: F1.GND, D1.cathode, C1.-, Q1.COLLECTOR
  N5: R1.Pin_1, Q1.BASE
  N6: D1.anode, Q1.EMITTER

custom parts:
  Fan - Ventilador: Ventilador de 2 pines, se encuentra comunmente en computadoras de escritorio
